# Fritzing sketch Controller (saved by Fritzing 0.9.3b)
breadboards: 1

parts:
  Componente1 = Arduino Uno (Rev3) - ICSP
  Part2 = Bluetooth HC-05 Macho
  U1 = Thumb Joystick [package=joystick]
  GY2 = MPU-6050 Board GY-521 [form="♀ (female)" package=THT]
  GY3 = MPU-6050 Board GY-521 [form="♀ (female)" package=THT]

nets:
  N1: Componente1.A0, U1.SEL+
  N2: Componente1.A1, U1.V+
  N3: Componente1.A4/SDA, GY2.pin4, GY3.pin4
  N4: Componente1.A5/SCL, GY2.pin3, GY3.pin3
  N5: Componente1.ICSP_MOSI, Componente1.D11_PWM/MOSI, Part2.RXD
  N6: Componente1.D2, GY2.pin8
  N7: Componente1.D3_PWM, U1.V-
  N8: Componente1.3V3, GY2.pin1, GY3.pin1, GY3.pin7
  N9: Componente1.5V, U1.H+
  N10: Componente1.GND, U1.SEL-, GY2.pin2, GY2.pin7, GY3.pin2

notes:
  Joystick
  MS: Rosa
  VRX: Celeste
  VRY: violeta
  GND: Negro
  5V: Rojo
  3.3V: Naranja
  SCL: Marrón
  SDA: Ocre
  MPU9250
  MPU6050

custom parts:
  MPU-6050 Board GY-521: Acelerometro y Giroscopio MPU-6050 Board GY-521
